# Fritzing sketch PIREN (saved by Fritzing 0.9.3b)
circuit board: 12.8cm x 9.7cm
breadboards: 1

parts:
  AUX = LED - 5mm [color="Red (633nm)" package="5 mm [THT]"]
  SIREN = LED - 5mm [color="Red (633nm)" package="5 mm [THT]"]
  GPIO = Header 12 [package=1x12_machine-pin-header_lock.004]
  POWER = female pin header, 2 pins [form="♀ (female)"]
  R1 = Resistor [tolerance=±5% resistance=220 package=THT]
  R2 = Resistor [tolerance=±5% resistance=220 package=THT]
  R3 = Resistor [tolerance=±5% resistance=10k package=THT]
  AUX_2 = Pushbutton [package=THT]
  R4 = Resistor [tolerance=±5% resistance=1k package=THT]
  R5 = Resistor [tolerance=±5% resistance=10k package=THT]
  R6 = Resistor [tolerance=±5% resistance=1k package=THT]
  LOOP = Pushbutton [package=THT]
  R7 = Resistor [tolerance=±5% resistance=10k package=THT]
  R8 = Resistor [tolerance=±5% resistance=1k package=THT]
  HORN = Pushbutton [package=THT]
  R9 = Resistor [tolerance=±5% resistance=10k package=THT]
  PIER = Pushbutton [package=THT]
  R10 = Resistor [tolerance=±5% resistance=1k package=THT]
  R11 = Resistor [tolerance=±5% resistance=10k package=THT]
  YELP = Pushbutton [package=THT]
  R12 = Resistor [tolerance=±5% resistance=1k package=THT]
  R13 = Resistor [tolerance=±5% resistance=10k package=THT]
  R14 = Resistor [tolerance=±5% resistance=1k package=THT]
  WAIL = Pushbutton [package=THT]
  R15 = Resistor [tolerance=±5% resistance=10k package=THT]
  R16 = Resistor [tolerance=±5% resistance=1k package=THT]
  PREV_M = Pushbutton [package=THT]
  R17 = Resistor [tolerance=±5% resistance=10k package=THT]
  R18 = Resistor [tolerance=±5% resistance=1k package=THT]
  NEXT_M = Pushbutton [package=THT]
  R19 = Resistor [tolerance=±5% resistance=10k package=THT]
  NEXT_B = Pushbutton [package=THT]
  R20 = Resistor [tolerance=±5% resistance=1k package=THT]
  R21 = Resistor [tolerance=±5% resistance=10k package=THT]
  R22 = Resistor [tolerance=±5% resistance=1k package=THT]
  PREV_B = Pushbutton [package=THT]
  GPIO2 = FTDI_BASIC [package=ftdi_basic]
  INTERFACE = FTDI_BASIC [package=ftdi_basic]

nets:
  N1: AUX.cathode, R2.Pin_0
  N2: AUX.anode, GPIO.2
  N3: SIREN.cathode, R1.Pin_0
  N4: SIREN.anode, GPIO.1
  N5: GPIO.3, R3.Pin_1, AUX_2.leg0
  N6: GPIO.4, R5.Pin_1, LOOP.leg0
  N7: GPIO.5, R7.Pin_1, HORN.leg0
  N8: GPIO.6, R9.Pin_1, PIER.leg0
  N9: GPIO.7, R11.Pin_1, YELP.leg0
  N10: GPIO.8, R13.Pin_1, WAIL.leg0
  N11: GPIO.9, R17.Pin_1, NEXT_M.leg0
  N12: GPIO.10, R15.Pin_1, PREV_M.leg0
  N13: GPIO.11, R19.Pin_1, NEXT_B.leg0
  N14: GPIO.12, R21.Pin_1, PREV_B.leg0
  N15: POWER.pin1, R4.Pin_0, R6.Pin_0, R8.Pin_0, R10.Pin_0, R12.Pin_0, R14.Pin_0, R16.Pin_0, R18.Pin_0, R20.Pin_0, R22.Pin_0
  N16: POWER.pin2, R1.Pin_1, R2.Pin_1, R3.Pin_0, R5.Pin_0, R7.Pin_0, R9.Pin_0, R11.Pin_0, R13.Pin_0, R15.Pin_0, R17.Pin_0, R19.Pin_0, R21.Pin_0
  N17: AUX_2.leg1, R4.Pin_1
  N18: R6.Pin_1, LOOP.leg1
  N19: R8.Pin_1, HORN.leg1
  N20: PIER.leg1, R10.Pin_1
  N21: YELP.leg1, R12.Pin_1
  N22: R14.Pin_1, WAIL.leg1
  N23: R16.Pin_1, PREV_M.leg1
  N24: R18.Pin_1, NEXT_M.leg1
  N25: NEXT_B.leg1, R20.Pin_1
  N26: R22.Pin_1, PREV_B.leg1
  N27: GPIO2.5, INTERFACE.5
  N28: GPIO2.1, INTERFACE.1
  N29: GPIO2.6, INTERFACE.6
  N30: GPIO2.2, INTERFACE.2
  N31: GPIO2.3, INTERFACE.3
  N32: GPIO2.4, INTERFACE.4

notes:
  +
  -
  Piren
  by Nice Lion Technologies
  www.github.com/nicelion/piren
  v0.1
  Copyright © 2017. Some Rights Reserved.
